# Fritzing sketch posture monitoring device (saved by Fritzing 0.9.3b)
breadboards: 1

parts:
  MH-ET_LIVE_ESP32_DEVKIT1 = MH-ET LIVE ESP32 DEVKIT 38 pins
  Part1 = InvenSense MPU6050
  U1 = Vibration Motor- ROB-08449 [package=vibe-motor-10mm]
  Q1 = NPN-Transistor [package="TO92 [THT]"]
  R1 = Resistor [tolerance=±5% resistance=1k package="0603 [SMD]"]
  D1 = Rectifier Diode [part_number=1N4001 package="300 mil [THT]"]

nets:
  3V3: MH-ET_LIVE_ESP32_DEVKIT1.3V3, Part1.VCC, U1.+, D1.cathode
  N1: MH-ET_LIVE_ESP32_DEVKIT1.GND#58, Q1.C
  N2: MH-ET_LIVE_ESP32_DEVKIT1.GND#64, Part1.GND
  N3: MH-ET_LIVE_ESP32_DEVKIT1.IO22, Part1.SCL
  N4: MH-ET_LIVE_ESP32_DEVKIT1.IO21, Part1.SDA
  N5: MH-ET_LIVE_ESP32_DEVKIT1.IO4, R1.Pin_1
  N6: U1.-, Q1.E, D1.anode
  N7: Q1.B, R1.Pin_0

custom parts:
  MH-ET LIVE ESP32 DEVKIT 38 pins: http://mh.nodebb.com/topic/2/mh-et-live-esp32-devkit
